# Fritzing sketch KARADIO WEB PLAYER (saved by Fritzing 0.9.3b)

parts:
  Part2 = Arduino MP3 Player Shield
  Gizwits_WiFi_Witty_ESP-12F1 = Gizwits WiFi Witty ESP-12F
  V1 = DC Power [voltage=5]
  NEXTION1 = NEXTION DISPLAY [package="NEXTION 7\""]

nets:
  VCC: Part2.VCC, Gizwits_WiFi_Witty_ESP-12F1.VCC, V1.V+, NEXTION1.+
  N1: Part2.MP3-DREQ, Gizwits_WiFi_Witty_ESP-12F1.GPIO5
  N2: Part2.5V-MP3-CS, Gizwits_WiFi_Witty_ESP-12F1.GPIO15
  N3: Part2.5V-MP3-RST, Gizwits_WiFi_Witty_ESP-12F1.GPIO0
  N4: Part2.5V-SD-CS, Gizwits_WiFi_Witty_ESP-12F1.GPIO4
  N5: Part2.5V-MOSI, Gizwits_WiFi_Witty_ESP-12F1.GPIO13
  N6: Part2.MISO, Gizwits_WiFi_Witty_ESP-12F1.GPIO12
  N7: Part2.5V-SCK, Gizwits_WiFi_Witty_ESP-12F1.GPIO14
  GND: Gizwits_WiFi_Witty_ESP-12F1.ADC, Gizwits_WiFi_Witty_ESP-12F1.GND, V1.V-, NEXTION1.GND
  N8: Gizwits_WiFi_Witty_ESP-12F1.RXD, NEXTION1.TXD
  N9: Gizwits_WiFi_Witty_ESP-12F1.TXD, NEXTION1.RXD

custom parts:
  NEXTION DISPLAY: INTELIGENT DISPLAY NEXTION 7"
